# Fritzing sketch sensors_connection_instruction (saved by Fritzing 0.8.7b)
breadboards: 1

parts:
  Mod1 = Raspberry Pi 4B
  M1 = MakerFocus MAX30102
  元件1 = Adafruit AHT20 Temperature and Humidity Sensor [part_number="Adafruit #4566"]

nets:
  5V: Mod1.5V, M1.VIN, 元件1.VCC
  N1: Mod1.GPIO2, M1.SCL, 元件1.SCL
  N2: Mod1.GPIO3, M1.SDA, 元件1.SDA
  GND: Mod1.GND, M1.GND, 元件1.GND

custom parts:
  MakerFocus MAX30102: Oximeter module using the MAX30102 chip. As usual, if you want the mounting holes in pcb, you need to drag a hole over the pad in silkscreen to actually drill the hole (by default they are not drilled)
  Adafruit AHT20 Temperature and Humidity Sensor: The AHT20 is a nice but inexpensive temperature and humidity sensor from the same folks that brought us the DHT22. You can take sensor readings as often as you like, and it uses standard I2C so its super easy to use with any Arduino or Linux/Raspberry Pi board. This sensor has a typical accuracy of +- 2% relative humidity, and +-0.3 °C. There is only one I2C address so its not a good option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
